# Fritzing sketch lucas_gokart (saved by Fritzing 0.9.9b)

parts:
  Mod1 = Nano-V3-0-IO-Expansion-Adapter
  Mod2 = KY-003 Hall Magnetic Sensor Module [package="Breakout board"]
  Mod3 = KY-003 Hall Magnetic Sensor Module [package="Breakout board"]
  M3 = DC Motor
  Part1 = Arduino Nano (Rev3.0)
  M4 = DC Motor
  BAT2 = 12 battery [package=battery]
  Cytron_Smart_drive_duo_60_motor_driver1 = MDDS60
  RE1 = Rotary Encoder [package=THT]
  R1 = Rotary Potentiometer (Small) [maximum_resistance=100kΩ package=THT]
  S1 = SWITCH-MOMENTARY-2 [package=tactile-pth-12mm]
  Part2 = LCD1602-I2C

nets:
  VCC: Mod1.VCC, Part1.5V, Cytron_Smart_drive_duo_60_motor_driver1.no_name_yet#connector_DIG1, R1.leg2, Part2.VCC
  VIN: Mod1.VIN, Part1.VIN
  N1: Mod1.A0, Part1.A0, R1.wiper
  GND: Mod1.GND, Mod3.-, Part1.GND, Cytron_Smart_drive_duo_60_motor_driver1.no_name_yet#connector_DIG2, R1.leg1, S1.1, Part2.GND
  N2: Mod1.D13/SCK, Part1.D13/SCK
  N3: Mod1.NC, Part1.3V3
  N4: Mod1.AREF, Part1.AREF
  N5: Mod1.A1, Part1.A1
  N6: Mod1.A2, Part1.A2
  N7: Mod1.A3, Part1.A3
  N8: Mod1.A4/SDA, Part1.A4, Part2.SDA
  N9: Mod1.A5/SCL, Part1.A5, Part2.SCL
  N10: Mod1.A6, Part1.A6
  N11: Mod1.A7, Part1.A7
  N12: Mod1.RST, Part1.RESET
  N13: Mod1.D12/MISO, Part1.D12/MISO, S1.2
  N14: Mod1.D11_PWM/MOSI, Part1.D11/MOSI, RE1.EncoderPinA
  N15: Mod1.D10_PWM/SS, Part1.D10, RE1.EncoderPinC
  N16: Mod1.D9_PWM, Part1.D9, RE1.EncoderPinB
  N17: Mod1.D8, Part1.D8
  N18: Mod1.D7, Part1.D7
  N19: Mod1.D6_PWM, Part1.D6
  N20: Mod1.D5_PWM, Part1.D5
  N21: Mod1.D4, Part1.D4
  N22: Mod1.D3_PWM, Mod3.S, Part1.D3
  N23: Mod1.D2, Mod2.S, Part1.D2
  N24: Mod1.D0/RX#64, Mod1.D1/TX#79, Mod1.D1/TX#83, Mod2.-, Part1.D0/RX
  VIN_2: Mod1.D1/TX#65, Mod1.D0/RX#78, Mod1.D0/RX#80, Mod2.Vin, Mod3.Vin, Part1.D1/TX
  N25: M3.pin_1, Cytron_Smart_drive_duo_60_motor_driver1.no_name_yet#connector_LB1
  N26: M3.pin_2, Cytron_Smart_drive_duo_60_motor_driver1.no_name_yet#connector_LA1
  N27: M4.pin_1, Cytron_Smart_drive_duo_60_motor_driver1.no_name_yet#connector_RB1
  N28: M4.pin_2, Cytron_Smart_drive_duo_60_motor_driver1.no_name_yet#connector_RA1
  N29: BAT2.-, Cytron_Smart_drive_duo_60_motor_driver1.no_name_yet#connector_VB2
  N30: BAT2.+, Cytron_Smart_drive_duo_60_motor_driver1.no_name_yet#connector_VB1

notes:
  Left Motor Hall Sensor
  Right Motor Hall Sensor
  24V Brushed DC Motor
  Arduino Nano + Expansion Board
  Digital Rotary Encoder
  (Steering Sensor)
  Potentiometer
  (Accelerator Pedal)
  Switch
  (Brake Pedal Sensor)
  16x2 LCD Status Display

custom parts:
  Nano-V3-0-IO-Expansion-Adapter: Nano V3.0 IO Expansion Adapter Shield. Note pcb view has been supressed as not useful. You can drag a Nano over the Nano connectors and it will connect and appear in schematic (although at present due to a bug, routing will not show as complete in breadboard).
  KY-003 Hall Magnetic Sensor Module: KEYES KY-003 Arduino Hall Magnetic Sensor Module is a switch that will turn on/off in the presence of a magnetic field.
  12 battery: 12V lead acid type battery, like the Husqvarna YTH2448 12V 35AH battery. This is the mini version 1/4 the size of the actual battery to be closer to typical breadboard parts (around 2in wide rathher than 7in). The pads in pcb are sized to accomidate up to 14ga wire (as these batterys will deliver high currents.)
  LCD1602-I2C: A standard character display, usually with 2x16 characters. Comes in many colors with LCM1602 IIC attached.
